# Fritzing sketch rgb-led (saved by Fritzing 0.9.0b)
breadboards: 1

parts:
  Arduino = Arduino Nano (Rev3.0)
  RGB_LED = RGB LED (com. anode, rbg) [package="5 mm [THT]"]
  DC_12V = Power plug
  QG = NPN-Transistor [package="TO92 [THT]"]
  QB = NPN-Transistor [package="TO92 [THT]"]
  QR = NPN-Transistor [package="TO92 [THT]"]
  RG = Rotary Potentiometer (Large) [maximum_resistance=100kΩ package=THT]
  RR = Rotary Potentiometer (Large) [maximum_resistance=100kΩ package=THT]
  RB = Rotary Potentiometer (Large) [maximum_resistance=100kΩ package=THT]

nets:
  GND: Arduino.GND, DC_12V.GND, QG.E, QB.E, QR.E
  N1: Arduino.D3, QG.B
  N2: Arduino.D5, QB.B
  N3: Arduino.D6, QR.B
  VIN: Arduino.VIN, RGB_LED.common_anode, DC_12V.VCC
  N4: Arduino.5V, RG.leg1, RR.leg1, RB.leg1
  N5: Arduino.A2, RB.wiper
  N6: Arduino.A1, RG.wiper
  N7: Arduino.A0, RR.wiper
  N8: RGB_LED.red_cathode, QR.C
  N9: RGB_LED.blue_cathode, QB.C
  N10: RGB_LED.green_cathode, QG.C
